// Logisim project Memory_game.circ as structural Verilog: 19 circuits, main circuit MemoryGame
module MemoryGame (
);

  wire A, a_t, B, b_t, bcd_to_7_segment_decoder_1_p1, binary_to_bcd_converter_1_p3, C, c_t, Checking, D, d_t,
       Enter_your_answer, Fail, OK, Remember_the_pattern, Right_or_Wrong, Start, Success;
  wire [3:0] main_1_score;

  Button button_1 (.out(Start));
  LED led_1 (.in(D));
  Button button_2 (.out(d_t));
  LED led_2 (.in(Fail));
  LED led_3 (.in(Success));
  LED led_4 (.in(A));
  LED led_5 (.in(C));
  Button button_3 (.out(a_t));
  Button button_4 (.out(c_t));
  LED led_6 (.in(B));
  Button button_5 (.out(b_t));
  main main_1 (
    .Start(Start), .button_1(a_t), .button_2(b_t), .button_3(c_t), .button_4(d_t), .score(main_1_score),
    .LED_1(A), .LED_2(B), .LED_3(C), .LED_4(D), .LED_fail(Fail), .LED_success(Success), .input_OK(OK),
    .showing(Remember_the_pattern), .input_wating(Enter_your_answer), .checking(Checking),
    .output_waiting(Right_or_Wrong));
  LED led_7 (.in(Remember_the_pattern));
  LED led_8 (.in(Enter_your_answer));
  LED led_9 (.in(Checking));
  LED led_10 (.in(Right_or_Wrong));
  LED led_11 (.in(OK));
  _7_Segment_Display u_7_segment_display_1 ();  // open: g, f, a, b, e, d, c, dp
  // BCD_to_7_Segment_decoder bcd_to_7_segment_decoder_1: pin names not known; wires that end beside it: bcd_to_7_segment_decoder_1_p1
  // Binary_to_BCD_converter #(.binvalue(4)) binary_to_bcd_converter_1: pin names not known; wires that end beside it: main_1_score, bcd_to_7_segment_decoder_1_p1, binary_to_bcd_converter_1_p3
  _7_Segment_Display u_7_segment_display_2 ();  // open: g, f, a, b, e, d, c, dp
  // BCD_to_7_Segment_decoder bcd_to_7_segment_decoder_2: pin names not known; wires that end beside it: binary_to_bcd_converter_1_p3

  // Notes on the sheet:
  //   Your Score
endmodule

module main (
  input  Start,
  input  button_1,
  input  button_2,
  input  button_3,
  input  button_4,
  output [3:0] score,
  output LED_1,
  output LED_2,
  output LED_3,
  output LED_4,
  output LED_fail,
  output LED_success,
  output input_OK,
  output showing,
  output input_wating,
  output checking,
  output output_waiting
);

  wire and_1_out, and_2_out, and_3_out, and_4_out, and_7_out, and_13_out, and_14_out, and_16_out, and_18_out,
       and_20_out, and_21_out, Answer_reset, clock_1_out, clock_2_out, clock_3_out, comparator_1_eq,
       comparator_2_eq, comparator_3_eq, comparator_4_eq, comparator_5_eq, comparator_6_eq, comparator_7_lt,
       comparator_8_eq, comparator_9_eq, comparator_10_eq, comparator_11_eq, comparator_12_eq,
       comparator_13_eq, comparator_14_eq, comparator_15_gt, comparator_16_gt, comparator_17_eq,
       comparator_18_eq, comparator_19_eq, comparator_20_eq, comparator_21_eq, comparator_22_eq,
       comparator_23_eq, comparator_24_eq, decoder_1_out0, decoder_1_out1, decoder_1_out2, decoder_1_out3,
       next_statement, not_1_out, not_2_out, not_3_out, not_4_out, not_5_out, not_6_out, not_7_out,
       not_8_out, not_9_out, not_10_out, not_11_out, not_12_out, not_13_out, not_14_out, NS1, NS2, NS3, NS4,
       or_2_out, or_3_out, or_4_out, or_5_out, or_6_out, or_7_out, or_8_out, or_9_out, or_10_out, or_11_out,
       or_12_out, or_14_out, P_enable, priority_encoder_1_p6, pulsegenerator_1_out_2, pulsegenerator_2_out_2,
       pulsegenerator_3_out_2, pulsegenerator_4_out_2, result, sound, twoclockdelay_1bit_4_out_3,
       twoclockdelay_1bit_5_out_3;
  wire [1:0] B_input, multiplexer_1_out, S_out, twoclockdelay_2bit_1_out_3;
  wire [3:0] c, InputCount_count_value, subtractor_1_out, synchronousfourbitscounter_1_out_2,
       synchronousfourbitscounter_2_out_2;
  wire [4:0] asyncronousfivebitscounter_1_count_value;
  wire [31:0] A, Answer, randompatterngenerater_1_random_value;

  Clock clock_1 (.out(clock_1_out));
  and and_1 (and_1_out, NS4, not_1_out);
  not not_1 (not_1_out, LED_fail);
  or or_1 (Answer_reset, Start, LED_success, LED_fail);
  Comparator #(.mode("unsigned"), .width(2)) comparator_1 (.a(S_out), .b(2'b00), .eq(comparator_1_eq));  // open: gt, lt
  Comparator #(.mode("unsigned"), .width(2)) comparator_2 (.a(S_out), .b(2'b01), .eq(comparator_2_eq));  // open: gt, lt
  Comparator #(.mode("unsigned"), .width(2)) comparator_3 (.a(S_out), .b(2'b10), .eq(comparator_3_eq));  // open: gt, lt
  Comparator #(.mode("unsigned"), .width(2)) comparator_4 (.a(S_out), .b(2'b11), .eq(comparator_4_eq));  // open: gt, lt
  or or_2 (or_2_out, Answer_reset, NS4);
  Multiplexer #(.select(4), .width(2)) multiplexer_1 (
    .in0(A[1:0]), .in1(A[3:2]), .in2(A[5:4]), .in3(A[7:6]), .in4(A[9:8]), .in5(A[11:10]), .in6(A[13:12]),
    .in7(A[15:14]), .in8(A[17:16]), .in9(A[19:18]), .in10(A[21:20]), .in11(A[23:22]), .in12(A[25:24]),
    .in13(A[27:26]), .in14(A[29:28]), .in15(A[31:30]), .out(multiplexer_1_out), .sel(c));
  AsyncronousFourBitsCounter InputCount (.clock(input_OK), .reset(or_3_out), .count_value(InputCount_count_value));
  Subtractor #(.width(4)) subtractor_1 (
    .a(InputCount_count_value), .b(4'b0001), .out(subtractor_1_out));  // open: bin, bout
  Comparator #(.mode("unsigned"), .width(2)) comparator_5 (.a(S_out), .b(2'b01), .eq(comparator_5_eq));  // open: gt, lt
  not not_2 (not_2_out, LED_fail);
  not not_3 (not_3_out, LED_success);
  and and_2 (and_2_out, not_2_out, not_3_out, comparator_1_eq);
  not not_4 (not_4_out, LED_fail);
  not not_5 (not_5_out, LED_success);
  and and_3 (and_3_out, not_4_out, not_5_out, comparator_2_eq);
  not not_6 (not_6_out, LED_fail);
  not not_7 (not_7_out, LED_success);
  and and_4 (and_4_out, not_6_out, not_7_out, comparator_3_eq);
  not not_8 (not_8_out, LED_fail);
  not not_9 (not_9_out, LED_success);
  and and_5 (output_waiting, not_8_out, not_9_out, comparator_4_eq);
  ButtonInput buttoninput_1 (
    .button_value(B_input), .reset(Answer_reset), .WE(input_OK), .stage_count(InputCount_count_value),
    .out_5(Answer[1:0]), .out_6(Answer[3:2]), .out_7(Answer[5:4]), .out_8(Answer[7:6]), .out_9(Answer[9:8]),
    .out_10(Answer[11:10]), .out_11(Answer[13:12]), .out_12(Answer[15:14]), .out_13(Answer[17:16]),
    .out_14(Answer[19:18]), .out_15(Answer[21:20]), .out_16(Answer[23:22]), .out_17(Answer[25:24]),
    .out_18(Answer[27:26]), .out_19(Answer[29:28]), .out_20(Answer[31:30]));
  Comparator #(.mode("unsigned"), .width(4)) comparator_6 (
    .a(subtractor_1_out), .b(score), .eq(comparator_6_eq));  // open: gt, lt
  and and_6 (NS2, comparator_6_eq, comparator_5_eq);
  TwoClockDelay_1bit twoclockdelay_1bit_1 (.in_1(and_2_out), .out_3(showing));  // open: in_2
  TwoClockDelay_1bit twoclockdelay_1bit_2 (.in_1(and_3_out), .out_3(input_wating));  // open: in_2
  TwoClockDelay_1bit twoclockdelay_1bit_3 (.in_1(and_4_out), .out_3(checking));  // open: in_2
  TwoClockDelay_2bit twoclockdelay_2bit_1 (.in_1(multiplexer_1_out), .in_2(NS4), .out_3(twoclockdelay_2bit_1_out_3));
  RandomPatternGenerater randompatterngenerater_1 (
    .start(Answer_reset), .random_value(randompatterngenerater_1_random_value));
  c_count c_count_1 (.enable(P_enable), .clock(clock_1_out), .reset(or_2_out), .count_value(c));
  StageCountResister stagecountresister_1 (.next_stage(and_1_out), .reset(Start), .stage_count(score));
  Comparator #(.mode("unsigned"), .width(4)) comparator_7 (.a(score), .b(c), .lt(comparator_7_lt));  // open: gt, eq
  not not_10 (not_10_out, comparator_7_lt);
  not not_11 (not_11_out, LED_fail);
  not not_12 (not_12_out, LED_success);
  or or_3 (or_3_out, NS4, Start);
  Pulse pulse_1 (.in_1(or_4_out), .out_2(input_OK));
  // Probe on Answer
  Register #(.width(32)) register_1 (
    .D(randompatterngenerater_1_random_value), .clk(Answer_reset), .Q(A));  // open: en, clr
  // Probe on score
  // Probe on c
  // Probe on S_out
  and and_7 (and_7_out, not_10_out, not_11_out, not_12_out);
  or or_4 (or_4_out, button_1, button_2, button_3, button_4);
  Comparator #(.mode("unsigned"), .width(4)) comparator_8 (.a(score), .b(c), .eq(comparator_8_eq));  // open: gt, lt
  Comparator #(.mode("unsigned"), .width(2)) comparator_9 (.a(2'b00), .b(S_out), .eq(comparator_9_eq));  // open: gt, lt
  Decoder #(.select(2)) decoder_1 (
    .out0(decoder_1_out0), .out1(decoder_1_out1), .out2(decoder_1_out2), .out3(decoder_1_out3),
    .sel(twoclockdelay_2bit_1_out_3), .en(or_5_out));
  PulseGenerator pulsegenerator_1 (.in_1(decoder_1_out0), .out_2(pulsegenerator_1_out_2));
  PulseGenerator pulsegenerator_2 (.in_1(decoder_1_out1), .out_2(pulsegenerator_2_out_2));
  and and_8 (LED_1, pulsegenerator_1_out_2, comparator_16_gt);
  and and_9 (LED_2, pulsegenerator_2_out_2, comparator_16_gt);
  // Priority_Encoder #(.select(2)) priority_encoder_1: pin names not known; wires that end beside it: button_1, button_2, B_input, button_3, button_4, priority_encoder_1_p6, priority_encoder_1_p6
  and and_10 (NS1, comparator_8_eq, comparator_9_eq);
  not not_13 (not_13_out, comparator_10_eq);
  Comparator #(.mode("unsigned"), .width(2)) comparator_10 (
    .a(S_out), .b(2'b11), .eq(comparator_10_eq));  // open: gt, lt
  TwoClockDelay_1bit twoclockdelay_1bit_4 (.in_1(and_7_out), .in_2(NS4), .out_3(twoclockdelay_1bit_4_out_3));
  PulseGenerator pulsegenerator_3 (.in_1(decoder_1_out2), .out_2(pulsegenerator_3_out_2));
  PulseGenerator pulsegenerator_4 (.in_1(decoder_1_out3), .out_2(pulsegenerator_4_out_2));
  and and_11 (LED_3, pulsegenerator_3_out_2, comparator_16_gt);
  and and_12 (LED_4, pulsegenerator_4_out_2, comparator_16_gt);
  and and_13 (and_13_out, not_13_out, twoclockdelay_1bit_4_out_3);
  buf or_5 (or_5_out, and_13_out);  // OR_Gate
  or or_6 (or_6_out, pulsegenerator_1_out_2, pulsegenerator_2_out_2, pulsegenerator_3_out_2, pulsegenerator_4_out_2);
  or or_7 (or_7_out, NS4, Start);
  or or_8 (or_8_out, LED_1, button_1);
  // Buzzer #(.smooth_level(3), .smooth_width(4)) buzzer_1: pin names not known; wires that end beside it: 14'h100, or_8_out, {7{1'b1}}
  or or_9 (or_9_out, LED_2, button_2);
  // Buzzer #(.smooth_level(3), .smooth_width(4)) buzzer_2: pin names not known; wires that end beside it: 14'h200, or_9_out, {7{1'b1}}
  or or_10 (or_10_out, LED_3, button_3);
  // Buzzer #(.smooth_level(3), .smooth_width(4)) buzzer_3: pin names not known; wires that end beside it: 14'h300, or_10_out, {7{1'b1}}
  or or_11 (or_11_out, LED_4, button_4);
  // Buzzer #(.smooth_level(3), .smooth_width(4)) buzzer_4: pin names not known; wires that end beside it: 14'h400, or_11_out, {7{1'b1}}
  AnswerCompare answercompare_1 (
    .statement(S_out), .stage_count(score), .A(A), .Answer(Answer), .cmp_result(result), .cmp_done(NS3));
  Comparator #(.mode("unsigned"), .width(2)) comparator_11 (
    .a(S_out), .b(2'b00), .eq(comparator_11_eq));  // open: gt, lt
  TwoClockDelay_1bit twoclockdelay_1bit_5 (.in_1(comparator_11_eq), .in_2(NS4), .out_3(twoclockdelay_1bit_5_out_3));
  Comparator #(.mode("unsigned"), .width(2)) comparator_12 (
    .a(S_out), .b(2'b10), .eq(comparator_12_eq));  // open: gt, lt
  Comparator #(.mode("unsigned"), .width(1)) comparator_13 (
    .a(result), .b(1'b0), .eq(comparator_13_eq));  // open: gt, lt
  Comparator #(.mode("unsigned"), .width(1)) comparator_14 (.a(NS3), .b(1'b1), .eq(comparator_14_eq));  // open: gt, lt
  not not_14 (not_14_out, comparator_15_gt);
  Comparator #(.mode("unsigned"), .width(4)) comparator_15 (.a(c), .b(score), .gt(comparator_15_gt));  // open: eq, lt
  // Probe on asyncronousfivebitscounter_1_count_value
  AsyncronousFiveBitsCounter asyncronousfivebitscounter_1 (
    .clock(or_6_out), .reset(or_7_out), .count_value(asyncronousfivebitscounter_1_count_value));
  FSM fsm_1 (.WE(next_statement), .reset(Start), .statement(S_out));
  and and_14 (and_14_out, comparator_12_eq, comparator_13_eq, comparator_14_eq);
  and and_15 (P_enable, not_14_out, twoclockdelay_1bit_5_out_3);
  Comparator #(.mode("unsigned"), .width(5)) comparator_16 (
    .a(asyncronousfivebitscounter_1_count_value), .b(5'b00001), .gt(comparator_16_gt));  // open: eq, lt
  // Buzzer #(.vol_width(2), .waveform("Sawtooth")) buzzer_5: pin names not known; wires that end beside it: 14'h100, and_14_out, 2'b11
  D_Flip_Flop d_ff_1 (.D(or_12_out), .clk(clock_2_out), .Q(LED_fail), .reset(Start));  // open: Qn, preset
  or or_12 (or_12_out, and_14_out, LED_fail);
  Clock clock_2 (.out(clock_2_out));
  Comparator #(.mode("unsigned"), .width(1)) comparator_17 (
    .a(result), .b(1'b1), .eq(comparator_17_eq));  // open: gt, lt
  Comparator #(.mode("unsigned"), .width(4)) comparator_18 (
    .a(score), .b(4'b1101), .eq(comparator_18_eq));  // open: gt, lt
  or or_13 (next_statement, NS1, NS2, NS3, NS4);
  and and_16 (and_16_out, comparator_17_eq, comparator_18_eq);
  D_Flip_Flop d_ff_2 (.D(or_14_out), .clk(clock_3_out), .Q(LED_success), .reset(Start));  // open: Qn, preset
  or or_14 (or_14_out, and_16_out, LED_success);
  Clock clock_3 (.out(clock_3_out));
  success_BGM success_bgm_1 (.suc(LED_success), .reset(Start));
  SynchronousFourBitsCounter synchronousfourbitscounter_1 (.reset(NS3), .out_2(synchronousfourbitscounter_1_out_2));
  Comparator #(.mode("unsigned"), .width(4)) comparator_19 (
    .a(synchronousfourbitscounter_1_out_2), .b(4'b0011), .eq(comparator_19_eq));  // open: gt, lt
  Comparator #(.mode("unsigned"), .width(2)) comparator_20 (
    .a(S_out), .b(2'b11), .eq(comparator_20_eq));  // open: gt, lt
  Comparator #(.mode("unsigned"), .width(1)) comparator_21 (
    .a(result), .b(1'b1), .eq(comparator_21_eq));  // open: gt, lt
  SynchronousFourBitsCounter synchronousfourbitscounter_2 (.reset(NS3), .out_2(synchronousfourbitscounter_2_out_2));
  and and_17 (NS4, comparator_19_eq, comparator_20_eq);
  and and_18 (and_18_out, comparator_20_eq, comparator_21_eq);
  Comparator #(.mode("unsigned"), .width(4)) comparator_22 (
    .a(score), .b(4'b1101), .eq(comparator_22_eq));  // open: gt, lt
  Comparator #(.mode("unsigned"), .width(4)) comparator_23 (
    .a(synchronousfourbitscounter_2_out_2), .b(4'b0000), .eq(comparator_23_eq));  // open: gt, lt
  Comparator #(.mode("unsigned"), .width(4)) comparator_24 (
    .a(synchronousfourbitscounter_2_out_2), .b(4'b0001), .eq(comparator_24_eq));  // open: gt, lt
  and and_19 (sound, and_18_out, ~comparator_22_eq);  // AND_Gate
  and and_20 (and_20_out, comparator_23_eq, sound);
  and and_21 (and_21_out, comparator_24_eq, sound);
  // Buzzer #(.vol_width(2), .waveform("Square")) buzzer_6: pin names not known; wires that end beside it: 14'h428, and_20_out, 2'b11
  // Buzzer #(.vol_width(2), .waveform("Square")) buzzer_7: pin names not known; wires that end beside it: 14'h310, and_21_out, 2'b11

  // Other names for the same wires on the sheet: fail = LED_fail; R = Start; S[3:0] = score; success = LED_success
endmodule

module RandomPatternGenerater (
  input  start,
  output [31:0] random_value
);

  Random #(.width(32)) random_1 (.clk(start), .out(random_value));  // open: clr, next
endmodule

module PulseGenerator (
  input  in_1,
  output out_2
);

  wire and_1_out, clock_1_out, d_ff_1_q;

  Clock clock_1 (.out(clock_1_out));
  D_Flip_Flop d_ff_1 (.D(clock_1_out), .clk(clock_1_out), .Q(d_ff_1_q));  // open: Qn, preset, reset
  and and_1 (and_1_out, clock_1_out, d_ff_1_q);
  and and_2 (out_2, and_1_out, in_1);
endmodule

module SynchronousFourBitsCounter (
  input  reset,
  output [3:0] out_2
);

  wire and_1_out, and_2_out, clock_1_out;

  Clock clock_1 (.out(clock_1_out));
  J_K_Flip_Flop j_k_ff_1 (.J(1'b1), .K(1'b1), .clk(clock_1_out), .Q(out_2[0]), .reset(reset));  // open: Qn, preset
  J_K_Flip_Flop j_k_ff_2 (
    .J(out_2[0]), .K(out_2[0]), .clk(clock_1_out), .Q(out_2[1]), .reset(reset));  // open: Qn, preset
  and and_1 (and_1_out, out_2[0], out_2[1]);
  J_K_Flip_Flop j_k_ff_3 (
    .J(and_1_out), .K(and_1_out), .clk(clock_1_out), .Q(out_2[2]), .reset(reset));  // open: Qn, preset
  and and_2 (and_2_out, and_1_out, out_2[2]);
  J_K_Flip_Flop j_k_ff_4 (
    .J(and_2_out), .K(and_2_out), .clk(clock_1_out), .Q(out_2[3]), .reset(reset));  // open: Qn, preset
endmodule

module AsyncronousFourBitsCounter (
  input  clock,
  input  reset,
  output [3:0] count_value
);

  wire and_1_out, and_2_out;

  J_K_Flip_Flop j_k_ff_1 (.J(1'b1), .K(1'b1), .clk(clock), .Q(count_value[0]), .reset(reset));  // open: Qn, preset
  J_K_Flip_Flop j_k_ff_2 (
    .J(count_value[0]), .K(count_value[0]), .clk(clock), .Q(count_value[1]), .reset(reset));  // open: Qn, preset
  and and_1 (and_1_out, count_value[0], count_value[1]);
  J_K_Flip_Flop j_k_ff_3 (
    .J(and_1_out), .K(and_1_out), .clk(clock), .Q(count_value[2]), .reset(reset));  // open: Qn, preset
  and and_2 (and_2_out, and_1_out, count_value[2]);
  J_K_Flip_Flop j_k_ff_4 (
    .J(and_2_out), .K(and_2_out), .clk(clock), .Q(count_value[3]), .reset(reset));  // open: Qn, preset
endmodule

module AsyncronousFiveBitsCounter (
  input  clock,
  input  reset,
  output [4:0] count_value
);

  wire and_1_out, and_2_out, and_3_out;

  J_K_Flip_Flop j_k_ff_1 (.J(1'b1), .K(1'b1), .clk(clock), .Q(count_value[0]), .reset(reset));  // open: Qn, preset
  J_K_Flip_Flop j_k_ff_2 (
    .J(count_value[0]), .K(count_value[0]), .clk(clock), .Q(count_value[1]), .reset(reset));  // open: Qn, preset
  and and_1 (and_1_out, count_value[0], count_value[1]);
  J_K_Flip_Flop j_k_ff_3 (
    .J(and_1_out), .K(and_1_out), .clk(clock), .Q(count_value[2]), .reset(reset));  // open: Qn, preset
  and and_2 (and_2_out, and_1_out, count_value[2]);
  J_K_Flip_Flop j_k_ff_4 (
    .J(and_2_out), .K(and_2_out), .clk(clock), .Q(count_value[3]), .reset(reset));  // open: Qn, preset
  buf and_3 (and_3_out, count_value[3]);  // AND_Gate
  J_K_Flip_Flop j_k_ff_5 (
    .J(and_3_out), .K(and_3_out), .clk(clock), .Q(count_value[4]), .reset(reset));  // open: Qn, preset
endmodule

module StageCountResister (
  input  next_stage,
  input  reset,
  output [3:0] stage_count
);

  wire clock_1_out, cmp_done_pulse_1_pulse_out;
  wire [3:0] pla_1_out;

  Register #(.width(4)) register_1 (
    .D(pla_1_out), .en(cmp_done_pulse_1_pulse_out), .clk(clock_1_out), .Q(stage_count), .clr(reset));
  cmp_done_pulse cmp_done_pulse_1 (.cmp_done_in(next_stage), .pulse_out(cmp_done_pulse_1_pulse_out));
  Clock clock_1 (.out(clock_1_out));
  PLA #(.in_width(4), .out_width(4), .\table ("0000 0001\n0001 0010\n0010 0011\n0011 0100\n0100 0101\n0101 0110\n0110 0111\n0111 1000\n1000 1001\n1001 1010\n1010 1011\n1011 1100\n1100 1101\n1101 1110\n1110 1111\n1111 0000")) pla_1 (
    .in(stage_count), .out(pla_1_out));
endmodule

module ButtonInput (
  input  [1:0] button_value,
  input  reset,
  input  WE,
  input  [3:0] stage_count,
  output [1:0] out_5,
  output [1:0] out_6,
  output [1:0] out_7,
  output [1:0] out_8,
  output [1:0] out_9,
  output [1:0] out_10,
  output [1:0] out_11,
  output [1:0] out_12,
  output [1:0] out_13,
  output [1:0] out_14,
  output [1:0] out_15,
  output [1:0] out_16,
  output [1:0] out_17,
  output [1:0] out_18,
  output [1:0] out_19,
  output [1:0] out_20
);

  wire decoder_1_out0, decoder_1_out1, decoder_1_out2, decoder_1_out3, decoder_1_out4, decoder_1_out5,
       decoder_1_out6, decoder_1_out7, decoder_1_out8, decoder_1_out9, decoder_1_out10, decoder_1_out11,
       decoder_1_out12, decoder_1_out13, decoder_1_out14, decoder_1_out15;

  Decoder #(.select(4)) decoder_1 (
    .out0(decoder_1_out0), .out1(decoder_1_out1), .out2(decoder_1_out2), .out3(decoder_1_out3),
    .out4(decoder_1_out4), .out5(decoder_1_out5), .out6(decoder_1_out6), .out7(decoder_1_out7),
    .out8(decoder_1_out8), .out9(decoder_1_out9), .out10(decoder_1_out10), .out11(decoder_1_out11),
    .out12(decoder_1_out12), .out13(decoder_1_out13), .out14(decoder_1_out14), .out15(decoder_1_out15),
    .sel(stage_count));  // open: en
  Register #(.width(2)) register_1 (.D(button_value), .en(decoder_1_out0), .clk(WE), .Q(out_5), .clr(reset));
  Register #(.width(2)) register_2 (.D(button_value), .en(decoder_1_out1), .clk(WE), .Q(out_6), .clr(reset));
  Register #(.width(2)) register_3 (.D(button_value), .en(decoder_1_out2), .clk(WE), .Q(out_7), .clr(reset));
  Register #(.width(2)) register_4 (.D(button_value), .en(decoder_1_out3), .clk(WE), .Q(out_8), .clr(reset));
  Register #(.width(2)) register_5 (.D(button_value), .en(decoder_1_out4), .clk(WE), .Q(out_9), .clr(reset));
  Register #(.width(2)) register_6 (.D(button_value), .en(decoder_1_out5), .clk(WE), .Q(out_10), .clr(reset));
  Register #(.width(2)) register_7 (.D(button_value), .en(decoder_1_out6), .clk(WE), .Q(out_11), .clr(reset));
  Register #(.width(2)) register_8 (.D(button_value), .en(decoder_1_out7), .clk(WE), .Q(out_12), .clr(reset));
  Register #(.width(2)) register_9 (.D(button_value), .en(decoder_1_out8), .clk(WE), .Q(out_13), .clr(reset));
  Register #(.width(2)) register_10 (.D(button_value), .en(decoder_1_out9), .clk(WE), .Q(out_14), .clr(reset));
  Register #(.width(2)) register_11 (.D(button_value), .en(decoder_1_out10), .clk(WE), .Q(out_15), .clr(reset));
  Register #(.width(2)) register_12 (.D(button_value), .en(decoder_1_out11), .clk(WE), .Q(out_16), .clr(reset));
  Register #(.width(2)) register_13 (.D(button_value), .en(decoder_1_out12), .clk(WE), .Q(out_17), .clr(reset));
  Register #(.width(2)) register_14 (.D(button_value), .en(decoder_1_out13), .clk(WE), .Q(out_18), .clr(reset));
  Register #(.width(2)) register_15 (.D(button_value), .en(decoder_1_out14), .clk(WE), .Q(out_19), .clr(reset));
  Register #(.width(2)) register_16 (.D(button_value), .en(decoder_1_out15), .clk(WE), .Q(out_20), .clr(reset));
endmodule

module FSM (
  input  WE,
  input  reset,
  output [1:0] statement
);

  wire clock_1_out;
  wire [1:0] pla_1_out;

  Clock clock_1 (.out(clock_1_out));
  PLA #(.\table ("00 01 # SHOWING\n01 10 # INPUT_WAITING\n10 11 # CHECKING\n11 00 # WAITING")) pla_1 (
    .in(statement), .out(pla_1_out));
  Register #(.width(2)) register_1 (.D(pla_1_out), .en(WE), .clk(clock_1_out), .Q(statement), .clr(reset));

  // Notes on the sheet:
  //   11 == wait
  //   00 == showing
  //   01 == Input waiting
  //   10 == check
endmodule

module AnswerCompare (
  input  [1:0] statement,
  input  [3:0] stage_count,
  input  [31:0] A,
  input  [31:0] Answer,
  output cmp_result,
  output cmp_done
);

  wire and_1_out, and_2_out, and_3_out, and_4_out, and_5_out, and_6_out, and_7_out, and_8_out, and_9_out,
       and_10_out, and_11_out, and_12_out, and_13_out, and_14_out, and_15_out, and_16_out, and_17_out,
       and_19_out, and_20_out, clock_1_out, clock_2_out, comparator_1_eq, comparator_2_eq, comparator_3_eq,
       comparator_4_eq, comparator_5_eq, comparator_6_eq, comparator_7_eq, comparator_8_eq, comparator_9_eq,
       comparator_10_eq, comparator_11_eq, comparator_12_eq, comparator_13_eq, comparator_14_eq,
       comparator_15_eq, comparator_16_eq, comparator_17_eq, comparator_17_gt, comparator_18_eq,
       comparator_18_gt, comparator_19_eq, comparator_19_gt, comparator_20_eq, comparator_20_gt,
       comparator_21_eq, comparator_21_gt, comparator_22_eq, comparator_22_gt, comparator_23_eq,
       comparator_23_gt, comparator_24_eq, comparator_24_gt, comparator_25_eq, comparator_25_gt,
       comparator_26_eq, comparator_26_gt, comparator_27_eq, comparator_27_gt, comparator_28_eq,
       comparator_28_gt, comparator_29_eq, comparator_29_gt, comparator_30_eq, comparator_30_gt,
       comparator_31_eq, comparator_31_gt, comparator_32_eq, comparator_32_gt, comparator_33_gt,
       comparator_34_eq, comparator_35_eq, comparator_36_eq, comparator_37_eq, d_ff_1_q, multiplexer_1_out,
       not_1_out, or_1_out, or_2_out, or_3_out, or_4_out, or_5_out, or_6_out, or_7_out, or_8_out, or_9_out,
       or_10_out, or_11_out, or_12_out, or_13_out, or_14_out, or_15_out, or_16_out;
  wire [3:0] match_counter_1_count_value, select_MUX;

  Comparator #(.width(2)) comparator_1 (.a(A[1:0]), .b(Answer[1:0]), .eq(comparator_1_eq));  // open: gt, lt
  Comparator #(.width(2)) comparator_2 (.a(A[3:2]), .b(Answer[3:2]), .eq(comparator_2_eq));  // open: gt, lt
  Comparator #(.width(2)) comparator_3 (.a(A[5:4]), .b(Answer[5:4]), .eq(comparator_3_eq));  // open: gt, lt
  Comparator #(.width(2)) comparator_4 (.a(A[7:6]), .b(Answer[7:6]), .eq(comparator_4_eq));  // open: gt, lt
  Comparator #(.width(2)) comparator_5 (.a(A[9:8]), .b(Answer[9:8]), .eq(comparator_5_eq));  // open: gt, lt
  Comparator #(.width(2)) comparator_6 (.a(A[11:10]), .b(Answer[11:10]), .eq(comparator_6_eq));  // open: gt, lt
  Comparator #(.width(2)) comparator_7 (.a(A[13:12]), .b(Answer[13:12]), .eq(comparator_7_eq));  // open: gt, lt
  Comparator #(.width(2)) comparator_8 (.a(A[15:14]), .b(Answer[15:14]), .eq(comparator_8_eq));  // open: gt, lt
  Comparator #(.width(2)) comparator_9 (.a(A[17:16]), .b(Answer[17:16]), .eq(comparator_9_eq));  // open: gt, lt
  Comparator #(.width(2)) comparator_10 (.a(A[19:18]), .b(Answer[19:18]), .eq(comparator_10_eq));  // open: gt, lt
  Comparator #(.width(2)) comparator_11 (.a(A[21:20]), .b(Answer[21:20]), .eq(comparator_11_eq));  // open: gt, lt
  Comparator #(.width(2)) comparator_12 (.a(A[23:22]), .b(Answer[23:22]), .eq(comparator_12_eq));  // open: gt, lt
  Comparator #(.width(2)) comparator_13 (.a(A[25:24]), .b(Answer[25:24]), .eq(comparator_13_eq));  // open: gt, lt
  Comparator #(.width(2)) comparator_14 (.a(A[27:26]), .b(Answer[27:26]), .eq(comparator_14_eq));  // open: gt, lt
  Comparator #(.width(2)) comparator_15 (.a(A[29:28]), .b(Answer[29:28]), .eq(comparator_15_eq));  // open: gt, lt
  Comparator #(.width(2)) comparator_16 (.a(A[31:30]), .b(Answer[31:30]), .eq(comparator_16_eq));  // open: gt, lt
  Comparator #(.mode("unsigned"), .width(4)) comparator_17 (
    .a(stage_count), .b(4'b0000), .gt(comparator_17_gt), .eq(comparator_17_eq));  // open: lt
  Comparator #(.mode("unsigned"), .width(4)) comparator_18 (
    .a(stage_count), .b(4'b0001), .gt(comparator_18_gt), .eq(comparator_18_eq));  // open: lt
  Comparator #(.mode("unsigned"), .width(4)) comparator_19 (
    .a(stage_count), .b(4'b0010), .gt(comparator_19_gt), .eq(comparator_19_eq));  // open: lt
  Comparator #(.mode("unsigned"), .width(4)) comparator_20 (
    .a(stage_count), .b(4'b0011), .gt(comparator_20_gt), .eq(comparator_20_eq));  // open: lt
  Comparator #(.mode("unsigned"), .width(4)) comparator_21 (
    .a(stage_count), .b(4'b0100), .gt(comparator_21_gt), .eq(comparator_21_eq));  // open: lt
  Comparator #(.mode("unsigned"), .width(4)) comparator_22 (
    .a(stage_count), .b(4'b0101), .gt(comparator_22_gt), .eq(comparator_22_eq));  // open: lt
  Comparator #(.mode("unsigned"), .width(4)) comparator_23 (
    .a(stage_count), .b(4'b0110), .gt(comparator_23_gt), .eq(comparator_23_eq));  // open: lt
  Comparator #(.mode("unsigned"), .width(4)) comparator_24 (
    .a(stage_count), .b(4'b0111), .gt(comparator_24_gt), .eq(comparator_24_eq));  // open: lt
  Comparator #(.mode("unsigned"), .width(4)) comparator_25 (
    .a(stage_count), .b(4'b1000), .gt(comparator_25_gt), .eq(comparator_25_eq));  // open: lt
  Comparator #(.mode("unsigned"), .width(4)) comparator_26 (
    .a(stage_count), .b(4'b1001), .gt(comparator_26_gt), .eq(comparator_26_eq));  // open: lt
  Comparator #(.mode("unsigned"), .width(4)) comparator_27 (
    .a(stage_count), .b(4'b1010), .gt(comparator_27_gt), .eq(comparator_27_eq));  // open: lt
  Comparator #(.mode("unsigned"), .width(4)) comparator_28 (
    .a(stage_count), .b(4'b1011), .gt(comparator_28_gt), .eq(comparator_28_eq));  // open: lt
  Comparator #(.mode("unsigned"), .width(4)) comparator_29 (
    .a(stage_count), .b(4'b1100), .gt(comparator_29_gt), .eq(comparator_29_eq));  // open: lt
  Comparator #(.mode("unsigned"), .width(4)) comparator_30 (
    .a(stage_count), .b(4'b1101), .gt(comparator_30_gt), .eq(comparator_30_eq));  // open: lt
  Comparator #(.mode("unsigned"), .width(4)) comparator_31 (
    .a(stage_count), .b(4'b1110), .gt(comparator_31_gt), .eq(comparator_31_eq));  // open: lt
  Comparator #(.mode("unsigned"), .width(4)) comparator_32 (
    .a(stage_count), .b(4'b1111), .gt(comparator_32_gt), .eq(comparator_32_eq));  // open: lt
  or or_1 (or_1_out, comparator_17_gt, comparator_17_eq);
  and and_1 (and_1_out, or_1_out, comparator_1_eq);
  or or_2 (or_2_out, comparator_18_gt, comparator_18_eq);
  and and_2 (and_2_out, or_2_out, comparator_2_eq);
  or or_3 (or_3_out, comparator_19_gt, comparator_19_eq);
  and and_3 (and_3_out, or_3_out, comparator_3_eq);
  or or_4 (or_4_out, comparator_20_gt, comparator_20_eq);
  and and_4 (and_4_out, or_4_out, comparator_4_eq);
  or or_5 (or_5_out, comparator_21_gt, comparator_21_eq);
  and and_5 (and_5_out, or_5_out, comparator_5_eq);
  or or_6 (or_6_out, comparator_22_gt, comparator_22_eq);
  and and_6 (and_6_out, or_6_out, comparator_6_eq);
  or or_7 (or_7_out, comparator_23_gt, comparator_23_eq);
  and and_7 (and_7_out, or_7_out, comparator_7_eq);
  or or_8 (or_8_out, comparator_24_gt, comparator_24_eq);
  and and_8 (and_8_out, or_8_out, comparator_8_eq);
  or or_9 (or_9_out, comparator_25_gt, comparator_25_eq);
  and and_9 (and_9_out, or_9_out, comparator_9_eq);
  or or_10 (or_10_out, comparator_26_gt, comparator_26_eq);
  and and_10 (and_10_out, or_10_out, comparator_10_eq);
  or or_11 (or_11_out, comparator_27_gt, comparator_27_eq);
  and and_11 (and_11_out, or_11_out, comparator_11_eq);
  or or_12 (or_12_out, comparator_28_gt, comparator_28_eq);
  and and_12 (and_12_out, or_12_out, comparator_12_eq);
  or or_13 (or_13_out, comparator_29_gt, comparator_29_eq);
  and and_13 (and_13_out, or_13_out, comparator_13_eq);
  or or_14 (or_14_out, comparator_30_gt, comparator_30_eq);
  and and_14 (and_14_out, or_14_out, comparator_14_eq);
  or or_15 (or_15_out, comparator_31_gt, comparator_31_eq);
  and and_15 (and_15_out, or_15_out, comparator_15_eq);
  or or_16 (or_16_out, comparator_32_gt, comparator_32_eq);
  and and_16 (and_16_out, or_16_out, comparator_16_eq);
  Multiplexer #(.select(4)) multiplexer_1 (
    .in0(and_1_out), .in1(and_2_out), .in2(and_3_out), .in3(and_4_out), .in4(and_5_out), .in5(and_6_out),
    .in6(and_7_out), .in7(and_8_out), .in8(and_9_out), .in9(and_10_out), .in10(and_11_out),
    .in11(and_12_out), .in12(and_13_out), .in13(and_14_out), .in14(and_15_out), .in15(and_16_out),
    .out(multiplexer_1_out), .sel(select_MUX));
  Comparator #(.mode("unsigned"), .width(4)) comparator_33 (
    .a(4'b1111), .b(select_MUX), .gt(comparator_33_gt));  // open: eq, lt
  Comparator #(.mode("unsigned"), .width(2)) comparator_34 (
    .a(statement), .b(2'b01), .eq(comparator_34_eq));  // open: gt, lt
  Clock clock_1 (.out(clock_1_out));
  Clock clock_2 (.out(clock_2_out));
  and and_17 (and_17_out, comparator_33_gt, clock_2_out, comparator_35_eq);
  Comparator #(.mode("unsigned"), .width(2)) comparator_35 (
    .a(statement), .b(2'b10), .eq(comparator_35_eq));  // open: gt, lt
  Comparator #(.mode("unsigned"), .width(2)) comparator_36 (
    .a(statement), .b(2'b01), .eq(comparator_36_eq));  // open: gt, lt
  D_Flip_Flop d_ff_1 (.D(comparator_37_eq), .clk(clock_1_out), .Q(d_ff_1_q));  // open: Qn, preset, reset
  Comparator #(.mode("unsigned"), .width(4)) comparator_37 (
    .a(select_MUX), .b(4'b1111), .eq(comparator_37_eq));  // open: gt, lt
  J_K_Flip_Flop j_k_ff_1 (
    .J(1'b1), .K(1'b1), .clk(and_17_out), .Q(select_MUX[0]), .reset(comparator_36_eq));  // open: Qn, preset
  not not_1 (not_1_out, d_ff_1_q);
  J_K_Flip_Flop j_k_ff_2 (
    .J(select_MUX[0]), .K(select_MUX[0]), .clk(and_17_out), .Q(select_MUX[1]), .reset(comparator_36_eq));  // open: Qn, preset
  match_counter match_counter_1 (
    .in_1(multiplexer_1_out), .reset(comparator_34_eq), .count_value(match_counter_1_count_value));
  and and_18 (cmp_done, not_1_out, comparator_37_eq);
  and and_19 (and_19_out, select_MUX[0], select_MUX[1]);
  J_K_Flip_Flop j_k_ff_3 (
    .J(and_19_out), .K(and_19_out), .clk(and_17_out), .Q(select_MUX[2]), .reset(comparator_36_eq));  // open: Qn, preset
  Comparator #(.mode("unsigned"), .width(4)) comparator_38 (
    .a(stage_count), .b(match_counter_1_count_value), .eq(cmp_result));  // open: gt, lt
  and and_20 (and_20_out, and_19_out, select_MUX[2]);
  J_K_Flip_Flop j_k_ff_4 (
    .J(and_20_out), .K(and_20_out), .clk(and_17_out), .Q(select_MUX[3]), .reset(comparator_36_eq));  // open: Qn, preset

  // Other names for the same wires on the sheet: stage[3:0] = stage_count
endmodule

module pulsegenerator_2 (
  input  next_stage,
  output next_stage_pulse
);

  wire clock_1_out, d_ff_1_q, d_ff_2_q, xor_1_out;

  D_Flip_Flop d_ff_1 (.D(next_stage), .clk(clock_1_out), .Q(d_ff_1_q));  // open: Qn, preset, reset
  Clock clock_1 (.out(clock_1_out));
  D_Flip_Flop d_ff_2 (.D(d_ff_1_q), .clk(clock_1_out), .Q(d_ff_2_q));  // open: Qn, preset, reset
  xor xor_1 (xor_1_out, d_ff_1_q, d_ff_2_q);
  and and_1 (next_stage_pulse, xor_1_out, d_ff_2_q);
endmodule

module match_counter (
  input  in_1,
  input  reset,
  output [3:0] count_value
);

  wire and_1_out, and_2_out, and_3_out, clock_1_out;

  Clock clock_1 (.out(clock_1_out));
  and and_1 (and_1_out, in_1, clock_1_out);
  J_K_Flip_Flop j_k_ff_1 (.J(1'b1), .K(1'b1), .clk(and_1_out), .Q(count_value[0]), .reset(reset));  // open: Qn, preset
  J_K_Flip_Flop j_k_ff_2 (
    .J(count_value[0]), .K(count_value[0]), .clk(and_1_out), .Q(count_value[1]), .reset(reset));  // open: Qn, preset
  and and_2 (and_2_out, count_value[0], count_value[1]);
  J_K_Flip_Flop j_k_ff_3 (
    .J(and_2_out), .K(and_2_out), .clk(and_1_out), .Q(count_value[2]), .reset(reset));  // open: Qn, preset
  and and_3 (and_3_out, and_2_out, count_value[2]);
  J_K_Flip_Flop j_k_ff_4 (
    .J(and_3_out), .K(and_3_out), .clk(and_1_out), .Q(count_value[3]), .reset(reset));  // open: Qn, preset
endmodule

module cmp_done_pulse (
  input  cmp_done_in,
  output pulse_out
);

  wire clock_1_out, d_ff_1_q, d_ff_2_q, not_1_out;

  D_Flip_Flop d_ff_1 (.D(cmp_done_in), .clk(clock_1_out), .Q(d_ff_1_q));  // open: Qn, preset, reset
  D_Flip_Flop d_ff_2 (.D(d_ff_1_q), .clk(clock_1_out), .Q(d_ff_2_q));  // open: Qn, preset, reset
  Clock clock_1 (.out(clock_1_out));
  not not_1 (not_1_out, d_ff_2_q);
  and and_1 (pulse_out, d_ff_1_q, not_1_out);
endmodule

module TwoClockDelay_1bit (
  input  in_1,
  input  in_2,
  output out_3
);

  wire clock_1_out, d_ff_1_q;

  Clock clock_1 (.out(clock_1_out));
  D_Flip_Flop d_ff_1 (.D(in_1), .clk(clock_1_out), .Q(d_ff_1_q), .reset(in_2));  // open: Qn, preset
  D_Flip_Flop d_ff_2 (.D(d_ff_1_q), .clk(clock_1_out), .Q(out_3), .reset(in_2));  // open: Qn, preset
endmodule

module TwoClockDelay_2bit (
  input  [1:0] in_1,
  input  in_2,
  output [1:0] out_3
);

  wire clock_1_out, d_ff_1_q, d_ff_2_q;

  Clock clock_1 (.out(clock_1_out));
  D_Flip_Flop d_ff_1 (.D(in_1[0]), .clk(clock_1_out), .Q(d_ff_1_q), .reset(in_2));  // open: Qn, preset
  D_Flip_Flop d_ff_2 (.D(in_1[1]), .clk(clock_1_out), .Q(d_ff_2_q), .reset(in_2));  // open: Qn, preset
  D_Flip_Flop d_ff_3 (.D(d_ff_1_q), .clk(clock_1_out), .Q(out_3[0]), .reset(in_2));  // open: Qn, preset
  D_Flip_Flop d_ff_4 (.D(d_ff_2_q), .clk(clock_1_out), .Q(out_3[1]), .reset(in_2));  // open: Qn, preset
endmodule

module c_count (
  input  enable,
  input  clock,
  input  reset,
  output [3:0] count_value
);

  wire and_1_out, and_2_out, and_3_out;

  J_K_Flip_Flop j_k_ff_1 (.J(1'b1), .K(1'b1), .clk(and_1_out), .Q(count_value[0]), .reset(reset));  // open: Qn, preset
  and and_1 (and_1_out, enable, clock);
  J_K_Flip_Flop j_k_ff_2 (
    .J(count_value[0]), .K(count_value[0]), .clk(and_1_out), .Q(count_value[1]), .reset(reset));  // open: Qn, preset
  and and_2 (and_2_out, count_value[0], count_value[1]);
  J_K_Flip_Flop j_k_ff_3 (
    .J(and_2_out), .K(and_2_out), .clk(and_1_out), .Q(count_value[2]), .reset(reset));  // open: Qn, preset
  and and_3 (and_3_out, and_2_out, count_value[2]);
  J_K_Flip_Flop j_k_ff_4 (
    .J(and_3_out), .K(and_3_out), .clk(and_1_out), .Q(count_value[3]), .reset(reset));  // open: Qn, preset
endmodule

module Pulse (
  input  in_1,
  output out_2
);

  wire clock_1_out, d_ff_1_q, not_1_out;

  Clock clock_1 (.out(clock_1_out));
  D_Flip_Flop d_ff_1 (.D(in_1), .clk(clock_1_out), .Q(d_ff_1_q));  // open: Qn, preset, reset
  not not_1 (not_1_out, d_ff_1_q);
  and and_1 (out_2, not_1_out, in_1);
endmodule

module success_BGM (
  input  suc,
  input  reset
);

  wire and_1_out, and_2_out, and_3_out, and_4_out, clock_1_out, clock_2_out, comparator_1_eq, d_ff_1_q,
       decoder_1_out1, decoder_1_out2, decoder_1_out3, decoder_1_out4, decoder_1_out5, decoder_1_out6,
       decoder_1_out7, decoder_1_out8, decoder_1_out9, decoder_1_out10, decoder_1_out11, decoder_1_out12,
       decoder_1_out13, decoder_1_out14, decoder_1_out15, decoder_1_out16, decoder_1_out17, decoder_1_out18,
       decoder_1_out19, decoder_1_out20, decoder_1_out21, decoder_1_out22, decoder_1_out23, decoder_1_out24,
       decoder_1_out25, decoder_1_out26, decoder_1_out27, decoder_1_out28, decoder_1_out29, decoder_1_out30,
       decoder_1_out31, or_1_out, or_2_out, or_3_out, or_4_out, or_5_out, stop;
  wire [4:0] j_k_ff_1_q, pla_1_out;

  and and_1 (and_1_out, suc, clock_1_out);
  Clock clock_1 (.out(clock_1_out));
  J_K_Flip_Flop j_k_ff_1 (
    .J(1'b1), .K(1'b1), .clk(and_1_out), .Q(j_k_ff_1_q[0]), .reset(or_1_out));  // open: Qn, preset
  or or_1 (or_1_out, stop, reset);
  Decoder #(.select(5)) decoder_1 (
    .out1(decoder_1_out1), .out2(decoder_1_out2), .out3(decoder_1_out3), .out4(decoder_1_out4),
    .out5(decoder_1_out5), .out6(decoder_1_out6), .out7(decoder_1_out7), .out8(decoder_1_out8),
    .out9(decoder_1_out9), .out10(decoder_1_out10), .out11(decoder_1_out11), .out12(decoder_1_out12),
    .out13(decoder_1_out13), .out14(decoder_1_out14), .out15(decoder_1_out15), .out16(decoder_1_out16),
    .out17(decoder_1_out17), .out18(decoder_1_out18), .out19(decoder_1_out19), .out20(decoder_1_out20),
    .out21(decoder_1_out21), .out22(decoder_1_out22), .out23(decoder_1_out23), .out24(decoder_1_out24),
    .out25(decoder_1_out25), .out26(decoder_1_out26), .out27(decoder_1_out27), .out28(decoder_1_out28),
    .out29(decoder_1_out29), .out30(decoder_1_out30), .out31(decoder_1_out31), .sel(pla_1_out));  // open: out0, en
  J_K_Flip_Flop j_k_ff_2 (
    .J(j_k_ff_1_q[0]), .K(j_k_ff_1_q[0]), .clk(and_1_out), .Q(j_k_ff_1_q[1]), .reset(or_1_out));  // open: Qn, preset
  and and_2 (and_2_out, j_k_ff_1_q[0], j_k_ff_1_q[1]);
  or or_2 (or_2_out, decoder_1_out31, decoder_1_out30);
  // Buzzer #(.waveform("Sawtooth")) buzzer_1: pin names not known; wires that end beside it: 14'h82d, or_2_out, {7{1'b1}}
  J_K_Flip_Flop j_k_ff_3 (
    .J(and_2_out), .K(and_2_out), .clk(and_1_out), .Q(j_k_ff_1_q[2]), .reset(or_1_out));  // open: Qn, preset
  // Buzzer #(.waveform("Sawtooth")) buzzer_2: pin names not known; wires that end beside it: 14'h7b8, decoder_1_out29, {7{1'b1}}
  and and_3 (and_3_out, and_2_out, j_k_ff_1_q[2]);
  J_K_Flip_Flop j_k_ff_4 (
    .J(and_3_out), .K(and_3_out), .clk(and_1_out), .Q(j_k_ff_1_q[3]), .reset(or_1_out));  // open: Qn, preset
  // Buzzer #(.waveform("Sawtooth")) buzzer_3: pin names not known; wires that end beside it: 14'h7b8, decoder_1_out28, {7{1'b1}}
  and and_4 (and_4_out, and_3_out, j_k_ff_1_q[3]);
  or or_3 (or_3_out, decoder_1_out26, decoder_1_out25);
  // Buzzer #(.waveform("Sawtooth")) buzzer_4: pin names not known; wires that end beside it: 14'h7b8, decoder_1_out27, {7{1'b1}}
  J_K_Flip_Flop j_k_ff_5 (
    .J(and_4_out), .K(and_4_out), .clk(and_1_out), .Q(j_k_ff_1_q[4]), .reset(or_1_out));  // open: Qn, preset
  // Buzzer #(.waveform("Sawtooth")) buzzer_5: pin names not known; wires that end beside it: 14'h749, or_3_out, {7{1'b1}}
  PLA #(.in_width(5), .out_width(5), .\table ("00000 00000\n00001 00001\n00010 00010\n00011 00011\n00100 00100\n00101 00101\n00110 00110\n00111 00111\n01000 01000\n01001 01001\n01010 01010\n01011 01011\n01100 01100\n01101 01101\n01110 01110\n01111 01111\n10000 10000\n10001 10001\n10010 10010\n10011 10011\n10100 10100\n10101 10101\n10110 10110\n10111 10111\n11000 11000\n11001 11001\n11010 11010\n11011 11011\n11100 11100\n11101 11101\n11110 11110\n11111 11111")) pla_1 (
    .in(j_k_ff_1_q), .out(pla_1_out));
  // Buzzer #(.waveform("Sawtooth")) buzzer_6: pin names not known; wires that end beside it: 14'h575, decoder_1_out24, {7{1'b1}}
  Comparator #(.mode("unsigned"), .width(5)) comparator_1 (
    .a(j_k_ff_1_q), .b({5{1'b1}}), .eq(comparator_1_eq));  // open: gt, lt
  // Buzzer #(.waveform("Sawtooth")) buzzer_7: pin names not known; wires that end beside it: 14'h497, decoder_1_out23, {7{1'b1}}
  D_Flip_Flop d_ff_1 (.D(comparator_1_eq), .clk(comparator_1_eq), .Q(d_ff_1_q), .reset(reset));  // open: Qn, preset
  // Buzzer #(.waveform("Sawtooth")) buzzer_8: pin names not known; wires that end beside it: 14'h2ba, decoder_1_out21, {7{1'b1}}
  // Buzzer #(.waveform("Sawtooth")) buzzer_9: pin names not known; wires that end beside it: 14'h3a4, decoder_1_out22, {7{1'b1}}
  // Buzzer #(.waveform("Sawtooth")) buzzer_10: pin names not known; wires that end beside it: 14'h24b, decoder_1_out20, {7{1'b1}}
  D_Flip_Flop d_ff_2 (.D(d_ff_1_q), .clk(clock_2_out), .Q(stop), .reset(reset));  // open: Qn, preset
  Clock clock_2 (.out(clock_2_out));
  or or_4 (or_4_out, decoder_1_out18, decoder_1_out17);
  // Buzzer #(.waveform("Sawtooth")) buzzer_11: pin names not known; wires that end beside it: 14'h19f, decoder_1_out19, {7{1'b1}}
  // Buzzer #(.waveform("Sawtooth")) buzzer_12: pin names not known; wires that end beside it: 14'h4dd, or_4_out, {7{1'b1}}
  // Buzzer #(.waveform("Sawtooth")) buzzer_13: pin names not known; wires that end beside it: 14'h67d, decoder_1_out16, {7{1'b1}}
  // Buzzer #(.waveform("Sawtooth")) buzzer_14: pin names not known; wires that end beside it: 14'h4dd, decoder_1_out15, {7{1'b1}}
  // Buzzer #(.waveform("Sawtooth")) buzzer_15: pin names not known; wires that end beside it: 14'h416, decoder_1_out14, {7{1'b1}}
  // Buzzer #(.waveform("Sawtooth")) buzzer_16: pin names not known; wires that end beside it: 14'h33f, decoder_1_out13, {7{1'b1}}
  // Buzzer #(.waveform("Sawtooth")) buzzer_17: pin names not known; wires that end beside it: 14'h20b, decoder_1_out11, {7{1'b1}}
  // Buzzer #(.waveform("Sawtooth")) buzzer_18: pin names not known; wires that end beside it: 14'h26e, decoder_1_out12, {7{1'b1}}
  // Buzzer #(.waveform("Sawtooth")) buzzer_19: pin names not known; wires that end beside it: 14'h19f, decoder_1_out10, {7{1'b1}}
  or or_5 (or_5_out, decoder_1_out9, decoder_1_out8);
  // Buzzer #(.waveform("Sawtooth")) buzzer_20: pin names not known; wires that end beside it: 14'h527, or_5_out, {7{1'b1}}
  // Buzzer #(.waveform("Sawtooth")) buzzer_21: pin names not known; wires that end beside it: 14'h620, decoder_1_out7, {7{1'b1}}
  // Buzzer #(.waveform("Sawtooth")) buzzer_22: pin names not known; wires that end beside it: 14'h620, decoder_1_out6, {7{1'b1}}
  // Buzzer #(.waveform("Sawtooth")) buzzer_23: pin names not known; wires that end beside it: 14'h527, decoder_1_out5, {7{1'b1}}
  // Buzzer #(.waveform("Sawtooth")) buzzer_24: pin names not known; wires that end beside it: 14'h310, decoder_1_out4, {7{1'b1}}
  // Buzzer #(.waveform("Sawtooth")) buzzer_25: pin names not known; wires that end beside it: 14'h293, decoder_1_out3, {7{1'b1}}
  // Buzzer #(.waveform("Sawtooth")) buzzer_26: pin names not known; wires that end beside it: 14'h188, decoder_1_out1, {7{1'b1}}
  // Buzzer #(.waveform("Sawtooth")) buzzer_27: pin names not known; wires that end beside it: 14'h20b, decoder_1_out2, {7{1'b1}}

  // Other names for the same wires on the sheet: enable = suc
endmodule
